# Fritzing sketch test_panel (saved by Fritzing 1.0.5)
breadboards: 2

parts:
  M2 = DOIT Esp32 DevKit v1 (30 pins long, 11 pins width) [part_number=ESP32S-PIN30]
  U3 = MCP23017 [package=dil28-3]
  M3 = DOIT Esp32 DevKit v1 (30 pins long, 11 pins width) [part_number=ESP32S-PIN30]
  part = Resistor [tolerance=±5% power=0.25W resistance=10k package=THT]
  R1 = Resistor [tolerance=±5% power=0.25W resistance=220 package=THT]
  LED1 = LED - 5mm [color="Red (633nm)" current=0.030A package="5 mm [THT]"]
  POWER = Taiway 100-SP-X-T1 SPDT Miniature Toggle Switch [part_number=0 package=THT]
  Q1 = NPN-Transistor [package="TO92 [THT]"]
  LCD1 = Waveshare 2.4in LCD display
  J1 = Piezo Speaker
  R3 = Resistor [tolerance=±5% resistance=220 package="2010 [SMD]"]
  Composant1 = Thumb Joystick
  MAP = Taiway 100-SP-X-T1 SPDT Miniature Toggle Switch [part_number=0 package=THT]

nets:
  VCC: M2.3V3, U3.VCC, LCD1.pin_1, Composant1.VCC
  GND: M2.GND, U3.GND, U3.A0, U3.A1, U3.A2, part.Pin_1, LED1.cathode, POWER.L1, Q1.C, LCD1.pin2, Composant1.GND
  N1: M2.D15, LCD1.pin_6
  N2: M2.RX2, M3.TX2
  N3: M2.TX2, M3.RX2
  N4: M2.D5, LCD1.pin_5
  N5: M2.D18, LCD1.pin4
  N6: M2.D21, U3.SDA
  N7: M2.D22, U3.SCL
  N8: M2.D23, LCD1.pin3
  N9: M2.D25, R3.Pin_0
  N10: M2.D27, Composant1.SEL
  N11: M2.D14, Composant1.HORZ
  N12: M2.D12, Composant1.VERT
  N13: M2.D13, LCD1.pin_7
  N14: M2.VIN, POWER.L2, J1.pin2, MAP.L1
  N15: U3.GPA6, MAP.L2
  N16: U3.GPA7, R1.Pin_1
  N17: U3.RESET, part.Pin_0
  N18: R1.Pin_0, LED1.anode
  N19: Q1.E, J1.pin1
  N20: Q1.B, R3.Pin_1

custom parts:
  DOIT Esp32 DevKit v1 (30 pins long, 11 pins width): The DOIT Esp32 DevKit v1 is one of the development board created by DOIT to evaluate the ESP-WROOM-32 module. It is based on the ESP32 microcontroller that boasts Wifi, Bluetooth, Ethernet and Low Power support all in a single chip. (vanepp) made breadboard work, adjusted pin numbering and labels and reduced size of schematic and cleaned up pcb. This chip is 30pins long (2 x15) and 11 pins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
  MCP23017: 16 bit I/O chip controlled via I2C
  Waveshare 2.4in LCD display: This is a generic 1.8 tft spi lcd display available on ebay and others. 240×320, General 2.4inch LCD Display Module, 65K RGB.
